# Fritzing sketch ScrabScrap (saved by Fritzing 0.9.4)
breadboards: 1

parts:
  Raspberry_Pi_1 = Raspberry Pi 3 [part_number=RPI-3-V1.2]
  R2 = Resistor [tolerance=±5% resistance=330 package=THT]
  LED1 = LED - 3mm [color="Green (555nm)" package="3 mm [THT]"]
  LED2 = LED - 3mm [color="Yellow (574nm)" package="3 mm [THT]"]
  R3 = Resistor [tolerance=±5% resistance=220 package=THT]
  R4 = Resistor [tolerance=±5% resistance=330 package=THT]
  R1 = Resistor [tolerance=±5% resistance=330 package=THT]
  S1 = Pushbutton [package="[THT]"]
  S2 = Pushbutton [package="[THT]"]
  S3 = Pushbutton [package="[THT]"]
  S4 = Pushbutton [package="[THT]"]
  Grove1 = Grove 4 Digit Display
  Grove2 = Grove 4 Digit Display
  LED4 = LED - 3mm [color="Red (633nm)" package="3 mm [THT]"]
  LED3 = LED - 3mm [color="Blue (430nm)" package="3 mm [THT]"]
  RTC = Real Time Clock Module - DS1307 RTC Breakout Board
  Reboot = Pushbutton [package="[THT]"]
  Reset = Pushbutton [package="[THT]"]
  Config = Pushbutton [package="[THT]"]

nets:
  3V3: Raspberry_Pi_1.3v3, Raspberry_Pi_1.3V3, RTC.5V
  N1: Raspberry_Pi_1.GPIO2, RTC.SDA
  N2: Raspberry_Pi_1.GPIO3, RTC.SCL
  N3: Raspberry_Pi_1.GPIO4, Reboot.Pin_3, Reboot.Pin_4
  N4: Raspberry_Pi_1.GPIO17, Reset.Pin_3, Reset.Pin_4
  N5: Raspberry_Pi_1.GPIO27, Config.Pin_1, Config.Pin_2
  GND: Raspberry_Pi_1.GND, R2.Pin_1, R3.Pin_1, R4.Pin_1, R1.Pin_1, S1.Pin_3, S1.Pin_4, S2.Pin_3, S2.Pin_4, S3.Pin_3, S3.Pin_4, S4.Pin_3, S4.Pin_4, Grove1.GND, Grove2.GND, RTC.GND, Reboot.Pin_1, Reboot.Pin_2, Reset.Pin_1, Reset.Pin_2, Config.Pin_3, Config.Pin_4
  N6: Raspberry_Pi_1.GPIO6, LED4.anode
  N7: Raspberry_Pi_1.GPIO13, LED2.anode
  N8: Raspberry_Pi_1.GPIO19, LED1.anode
  N9: Raspberry_Pi_1.GPIO26, LED3.anode
  N10: Raspberry_Pi_1.GPIO21, S1.Pin_1, S1.Pin_2
  N11: Raspberry_Pi_1.GPIO20, S2.Pin_1, S2.Pin_2
  N12: Raspberry_Pi_1.GPIO16, S4.Pin_1, S4.Pin_2
  N13: Raspberry_Pi_1.GPIO12, S3.Pin_1, S3.Pin_2
  N14: Raspberry_Pi_1.GPIO25, Grove2.DIO
  N15: Raspberry_Pi_1.GPIO24, Grove2.CLK
  N16: Raspberry_Pi_1.GPIO23, Grove1.DIO
  N17: Raspberry_Pi_1.GPIO18, Grove1.CLK
  VCC: Raspberry_Pi_1.5V, Grove1.VCC, Grove2.VCC
  N18: R2.Pin_0, LED1.cathode
  N19: LED2.cathode, R3.Pin_0
  N20: R4.Pin_0, LED4.cathode
  N21: R1.Pin_0, LED3.cathode
